// Logisim project riscv.circ as structural Verilog: 2 circuits, main circuit main
module main (
  input  in_1
);

  wire CLK, RESET;
  wire [7:0] counter_1_q, IRAM_data;
  wire [31:0] register_1_q;

  Clock clock_1 (.out(CLK));
  Counter counter_1 (.clr(RESET), .clk(CLK), .Q(counter_1_q));  // open: load, up, count, D, carry
  _7_Segment_Display u_7_segment_display_1 ();  // open: g, f, a, b, e, d, c, dp
  // BCD_to_7_Segment_decoder bcd_to_7_segment_decoder_1: pin names not known
  // Binairy_to_BCD_converter #(.binvalue(8)) binairy_to_bcd_converter_1: pin names not known; wires that end beside it: counter_1_q
  _7_Segment_Display u_7_segment_display_2 ();  // open: g, f, a, b, e, d, c, dp
  // BCD_to_7_Segment_decoder bcd_to_7_segment_decoder_2: pin names not known
  POR por_1 (.out(RESET));
  ROM IRAM (.addr(counter_1_q), .data(IRAM_data));
  Register register_1 (.D(IRAM_data), .en(in_1), .clk(CLK), .Q(register_1_q[7:0]));  // open: clr
  register_file register_file_1 (
    .CLK(CLK), .i_read_sel_1(register_1_q[19:15]), .i_read_sel_2(register_1_q[24:20]));  // open: i_write_data, i_write_sel, i_we, RESET, o_read_data_2, o_read_data_1
  // Pins of 8 and 32 bits meet at register_1_q

  // Notes on the sheet:
  //   contents of IRAM (hex, n*v repeats v):
  //   0 0 3 e3
endmodule

module register_file (
  input  CLK,
  input  [4:0] i_read_sel_1,
  input  [4:0] i_read_sel_2,
  input  [31:0] i_write_data,
  input  [4:0] i_write_sel,
  input  i_we,
  input  RESET,
  output [31:0] o_read_data_2,
  output [31:0] o_read_data_1
);

  wire demultiplexer_1_out1, demultiplexer_1_out2, demultiplexer_1_out3, demultiplexer_1_out4,
       demultiplexer_1_out5, demultiplexer_1_out6, demultiplexer_1_out7, demultiplexer_1_out8,
       demultiplexer_1_out9, demultiplexer_1_out10, demultiplexer_1_out11, demultiplexer_1_out12,
       demultiplexer_1_out13, demultiplexer_1_out14, demultiplexer_1_out15, demultiplexer_1_out16,
       demultiplexer_1_out17, demultiplexer_1_out18, demultiplexer_1_out19, demultiplexer_1_out20,
       demultiplexer_1_out21, demultiplexer_1_out22, demultiplexer_1_out23, demultiplexer_1_out24,
       demultiplexer_1_out25, demultiplexer_1_out26, demultiplexer_1_out27, demultiplexer_1_out28,
       demultiplexer_1_out29, demultiplexer_1_out30, demultiplexer_1_out31;
  wire [31:0] register_1_q, register_2_q, register_3_q, register_4_q, register_5_q, register_6_q,
       register_7_q, register_8_q, register_9_q, register_10_q, register_11_q, register_12_q, register_13_q,
       register_14_q, register_15_q, register_16_q, register_17_q, register_18_q, register_19_q,
       register_20_q, register_21_q, register_22_q, register_23_q, register_24_q, register_25_q,
       register_26_q, register_27_q, register_28_q, register_29_q, register_30_q, register_31_q,
       register_32_q;

  Demultiplexer #(.enable("false"), .select(5)) demultiplexer_1 (
    .out1(demultiplexer_1_out1), .out2(demultiplexer_1_out2), .out3(demultiplexer_1_out3),
    .out4(demultiplexer_1_out4), .out5(demultiplexer_1_out5), .out6(demultiplexer_1_out6),
    .out7(demultiplexer_1_out7), .out8(demultiplexer_1_out8), .out9(demultiplexer_1_out9),
    .out10(demultiplexer_1_out10), .out11(demultiplexer_1_out11), .out12(demultiplexer_1_out12),
    .out13(demultiplexer_1_out13), .out14(demultiplexer_1_out14), .out15(demultiplexer_1_out15),
    .out16(demultiplexer_1_out16), .out17(demultiplexer_1_out17), .out18(demultiplexer_1_out18),
    .out19(demultiplexer_1_out19), .out20(demultiplexer_1_out20), .out21(demultiplexer_1_out21),
    .out22(demultiplexer_1_out22), .out23(demultiplexer_1_out23), .out24(demultiplexer_1_out24),
    .out25(demultiplexer_1_out25), .out26(demultiplexer_1_out26), .out27(demultiplexer_1_out27),
    .out28(demultiplexer_1_out28), .out29(demultiplexer_1_out29), .out30(demultiplexer_1_out30),
    .out31(demultiplexer_1_out31), .in(i_we), .sel(i_write_sel));  // open: out0
  Register #(.width(32)) register_1 (.D(i_write_data), .en(1'b0), .clk(CLK), .Q(register_1_q), .clr(RESET));
  Register #(.width(32)) register_2 (
    .D(i_write_data), .en(demultiplexer_1_out1), .clk(CLK), .Q(register_2_q), .clr(RESET));
  Register #(.width(32)) register_3 (
    .D(i_write_data), .en(demultiplexer_1_out2), .clk(CLK), .Q(register_3_q), .clr(RESET));
  Register #(.width(32)) register_4 (
    .D(i_write_data), .en(demultiplexer_1_out3), .clk(CLK), .Q(register_4_q), .clr(RESET));
  Register #(.width(32)) register_5 (
    .D(i_write_data), .en(demultiplexer_1_out4), .clk(CLK), .Q(register_5_q), .clr(RESET));
  Register #(.width(32)) register_6 (
    .D(i_write_data), .en(demultiplexer_1_out5), .clk(CLK), .Q(register_6_q), .clr(RESET));
  Register #(.width(32)) register_7 (
    .D(i_write_data), .en(demultiplexer_1_out6), .clk(CLK), .Q(register_7_q), .clr(RESET));
  Register #(.width(32)) register_8 (
    .D(i_write_data), .en(demultiplexer_1_out7), .clk(CLK), .Q(register_8_q), .clr(RESET));
  Register #(.width(32)) register_9 (
    .D(i_write_data), .en(demultiplexer_1_out8), .clk(CLK), .Q(register_9_q), .clr(RESET));
  Register #(.width(32)) register_10 (
    .D(i_write_data), .en(demultiplexer_1_out9), .clk(CLK), .Q(register_10_q), .clr(RESET));
  Register #(.width(32)) register_11 (
    .D(i_write_data), .en(demultiplexer_1_out10), .clk(CLK), .Q(register_11_q), .clr(RESET));
  Register #(.width(32)) register_12 (
    .D(i_write_data), .en(demultiplexer_1_out11), .clk(CLK), .Q(register_12_q), .clr(RESET));
  Register #(.width(32)) register_13 (
    .D(i_write_data), .en(demultiplexer_1_out12), .clk(CLK), .Q(register_13_q), .clr(RESET));
  Register #(.width(32)) register_14 (
    .D(i_write_data), .en(demultiplexer_1_out13), .clk(CLK), .Q(register_14_q), .clr(RESET));
  Register #(.width(32)) register_15 (
    .D(i_write_data), .en(demultiplexer_1_out14), .clk(CLK), .Q(register_15_q), .clr(RESET));
  Register #(.width(32)) register_16 (
    .D(i_write_data), .en(demultiplexer_1_out15), .clk(CLK), .Q(register_16_q), .clr(RESET));
  Register #(.width(32)) register_17 (
    .D(i_write_data), .en(demultiplexer_1_out16), .clk(CLK), .Q(register_17_q), .clr(RESET));
  Register #(.width(32)) register_18 (
    .D(i_write_data), .en(demultiplexer_1_out17), .clk(CLK), .Q(register_18_q), .clr(RESET));
  Register #(.width(32)) register_19 (
    .D(i_write_data), .en(demultiplexer_1_out18), .clk(CLK), .Q(register_19_q), .clr(RESET));
  Register #(.width(32)) register_20 (
    .D(i_write_data), .en(demultiplexer_1_out19), .clk(CLK), .Q(register_20_q), .clr(RESET));
  Register #(.width(32)) register_21 (
    .D(i_write_data), .en(demultiplexer_1_out20), .clk(CLK), .Q(register_21_q), .clr(RESET));
  Register #(.width(32)) register_22 (
    .D(i_write_data), .en(demultiplexer_1_out21), .clk(CLK), .Q(register_22_q), .clr(RESET));
  Register #(.width(32)) register_23 (
    .D(i_write_data), .en(demultiplexer_1_out22), .clk(CLK), .Q(register_23_q), .clr(RESET));
  Register #(.width(32)) register_24 (
    .D(i_write_data), .en(demultiplexer_1_out23), .clk(CLK), .Q(register_24_q), .clr(RESET));
  Register #(.width(32)) register_25 (
    .D(i_write_data), .en(demultiplexer_1_out24), .clk(CLK), .Q(register_25_q), .clr(RESET));
  Register #(.width(32)) register_26 (
    .D(i_write_data), .en(demultiplexer_1_out25), .clk(CLK), .Q(register_26_q), .clr(RESET));
  Register #(.width(32)) register_27 (
    .D(i_write_data), .en(demultiplexer_1_out26), .clk(CLK), .Q(register_27_q), .clr(RESET));
  Register #(.width(32)) register_28 (
    .D(i_write_data), .en(demultiplexer_1_out27), .clk(CLK), .Q(register_28_q), .clr(RESET));
  Register #(.width(32)) register_29 (
    .D(i_write_data), .en(demultiplexer_1_out28), .clk(CLK), .Q(register_29_q), .clr(RESET));
  Register #(.width(32)) register_30 (
    .D(i_write_data), .en(demultiplexer_1_out29), .clk(CLK), .Q(register_30_q), .clr(RESET));
  Register #(.width(32)) register_31 (
    .D(i_write_data), .en(demultiplexer_1_out30), .clk(CLK), .Q(register_31_q), .clr(RESET));
  Register #(.width(32)) register_32 (
    .D(i_write_data), .en(demultiplexer_1_out31), .clk(CLK), .Q(register_32_q), .clr(RESET));
  Multiplexer #(.enable("false"), .select(5), .width(32)) multiplexer_1 (
    .in0(register_1_q), .in1(register_2_q), .in2(register_3_q), .in3(register_4_q), .in4(register_5_q),
    .in5(register_6_q), .in6(register_7_q), .in7(register_8_q), .in8(register_9_q), .in9(register_10_q),
    .in10(register_11_q), .in11(register_12_q), .in12(register_13_q), .in13(register_14_q),
    .in14(register_15_q), .in15(register_16_q), .in16(register_17_q), .in17(register_18_q),
    .in18(register_19_q), .in19(register_20_q), .in20(register_21_q), .in21(register_22_q),
    .in22(register_23_q), .in23(register_24_q), .in24(register_25_q), .in25(register_26_q),
    .in26(register_27_q), .in27(register_28_q), .in28(register_29_q), .in29(register_30_q),
    .in30(register_31_q), .in31(register_32_q), .out(o_read_data_2), .sel(i_read_sel_2));
  Multiplexer #(.enable("false"), .select(5), .width(32)) multiplexer_2 (
    .in0(register_1_q), .in1(register_2_q), .in2(register_3_q), .in3(register_4_q), .in4(register_5_q),
    .in5(register_6_q), .in6(register_7_q), .in7(register_8_q), .in8(register_9_q), .in9(register_10_q),
    .in10(register_11_q), .in11(register_12_q), .in12(register_13_q), .in13(register_14_q),
    .in14(register_15_q), .in15(register_16_q), .in16(register_17_q), .in17(register_18_q),
    .in18(register_19_q), .in19(register_20_q), .in20(register_21_q), .in21(register_22_q),
    .in22(register_23_q), .in23(register_24_q), .in24(register_25_q), .in25(register_26_q),
    .in26(register_27_q), .in27(register_28_q), .in28(register_29_q), .in29(register_30_q),
    .in30(register_31_q), .in31(register_32_q), .out(o_read_data_1), .sel(i_read_sel_1));
endmodule
